// Logisim project SAP1_manual.circ as structural Verilog: 15 circuits, main circuit main
module main (
  input  in_1,
  input  in_2,
  input  in_3,
  input  in_4,
  input  in_5,
  input  in_6,
  input  in_7,
  input  [7:0] in_8,
  output [7:0] out_9,
  output [3:0] out_10,
  output [7:0] out_11,
  output [7:0] out_12,
  output [7:0] out_13,
  output [7:0] out_14,
  output [7:0] out_15,
  output [7:0] out_16,
  output [7:0] out_17,
  output [7:0] out_18,
  output [7:0] out_19,
  output [7:0] out_20,
  output [7:0] out_21,
  output [7:0] out_22,
  output [7:0] out_23,
  output [7:0] out_24,
  output [7:0] out_25,
  output [7:0] out_26,
  output [7:0] out_27,
  output [7:0] out_28,
  output [7:0] out_29,
  output [7:0] out_30,
  output [3:0] out_31,
  output [3:0] out_32,
  output [7:0] out_33
);

  wire a_in, address_out_en, alu_out, alu_sub, b_in, button_1_out, hlt_set, ins_reg_in_en, mar_in_en, pc_en,
       pc_load, pc_out, right_or_left, ro_out_en, rotate_reg_en, sram_rd, sram_wr;

  pc_with_loader pc_with_loader_1 (
    .pc_en(pc_en), .pc_in(out_10), .pc_load(pc_load), .clk(in_7), .pc_reset(in_1), .pc_out_en(pc_out),
    .pc_out(out_10));
  sram sram_1 (
    .sram_rd(sram_rd), .sram_wr(sram_wr), .sram_d_in({out_12[7:4], out_10}),
    .mar_d_in({out_12[7:4], out_10}), .mar_in_en(mar_in_en), .sram_clk(in_7), .out_7({out_12[7:4], out_10}),
    .out_8(out_14), .out_9(out_15), .out_10(out_16), .out_11(out_17), .out_12(out_18), .out_13(out_19),
    .out_14(out_21), .out_15(out_22), .out_16(out_23), .out_17(out_24), .out_18(out_25), .out_19(out_26),
    .out_20(out_27), .out_21(out_28), .out_22(out_29), .out_23(out_30));
  assign {out_12[7:4], out_10} = in_3 ? in_8 : 8'bz;  // Controlled_Buffer controlled_buffer_1
  reg_gp reg_gp_1 (
    .reg_in({out_12[7:4], out_10}), .reg_in_en(a_in), .reg_clk(in_7), .reg_out_en(in_4),
    .reg_int_out(out_11), .reg_out({out_12[7:4], out_10}));
  reg_gp reg_gp_2 (
    .reg_in({out_12[7:4], out_10}), .reg_in_en(b_in), .reg_clk(in_7), .reg_out_en(in_5),
    .reg_int_out(out_20), .reg_out({out_12[7:4], out_10}));
  ins_reg ins_reg_1 (
    .ins_reg_in({out_12[7:4], out_10}), .ins_reg_in_en(ins_reg_in_en), .clk(in_7),
    .address_out_en(address_out_en), .add_outs(out_10), .ins_out(out_32));
  Shifter8 shifter8_1 (
    .B_reg_int_out(out_20), .A_reg_int_out(out_11), .rotate_reg_en(rotate_reg_en),
    .right_or_left(right_or_left), .ro_out_en(ro_out_en), .ro_out(out_9));
  alu alu_1 (
    .alu_in_1(out_11), .alu_out_en(alu_out), .alu_sub(alu_sub), .alu_in_2(out_20),
    .alu_out({out_12[7:4], out_10}));  // open: alu_carry_out
  Button button_1 (.out(button_1_out));
  cs cs_1 (
    .clk(in_7), .timig_reset(in_1), .opcode(out_32), .switch(button_1_out), .mar_in_manual(in_2),
    .debug(in_3), .sram_wr_manual(in_6), .pc_en(pc_en), .alu_sub(alu_sub), .mar_in_en(mar_in_en),
    .sram_rd(sram_rd), .pc_out(pc_out), .ins_reg_in_en(ins_reg_in_en), .a_in(a_in), .b_in(b_in),
    .ro_out_en(ro_out_en), .pc_load(pc_load), .hlt_set(hlt_set), .rotate_reg_en(rotate_reg_en),
    .right_or_left(right_or_left), .sram_wr(sram_wr), .alu_out(alu_out), .address_out_en(address_out_en));

  assign out_12[3:0] = out_10;
  assign out_13 = {out_12[7:4], out_10};
  assign out_31 = out_10;
  assign out_33 = {out_12[7:4], out_10};

  // Other names for the same wires on the sheet: a_out = in_4; b_out = in_5; clk = in_7; debug = in_3;
  //   debug_data[7:0] = in_8; mar_in_manual = in_2; pc_reset = in_1; sram_wr_manual = in_6

  // Notes on the sheet:
  //   Debugging data into RAM
  //   constant
endmodule

module reg_gp (
  input  [7:0] reg_in,
  input  reg_in_en,
  input  reg_clk,
  input  reg_out_en,
  output [7:0] reg_int_out,
  output [7:0] reg_out
);

  wire multiplexer_1_out, multiplexer_2_out, multiplexer_3_out, multiplexer_4_out, multiplexer_5_out,
       multiplexer_6_out, multiplexer_7_out, multiplexer_8_out;

  Multiplexer multiplexer_1 (.in0(reg_int_out[7]), .in1(reg_in[7]), .out(multiplexer_1_out), .sel(reg_in_en));
  D_Flip_Flop d_ff_1 (.D(multiplexer_1_out), .clk(reg_clk), .Q(reg_int_out[7]));  // open: Qn, preset, reset
  assign reg_out[7] = reg_out_en ? reg_int_out[7] : 1'bz;  // Controlled_Buffer controlled_buffer_1
  Multiplexer multiplexer_2 (.in0(reg_int_out[6]), .in1(reg_in[6]), .out(multiplexer_2_out), .sel(reg_in_en));
  D_Flip_Flop d_ff_2 (.D(multiplexer_2_out), .clk(reg_clk), .Q(reg_int_out[6]));  // open: Qn, preset, reset
  assign reg_out[6] = reg_out_en ? reg_int_out[6] : 1'bz;  // Controlled_Buffer controlled_buffer_2
  Multiplexer multiplexer_3 (.in0(reg_int_out[5]), .in1(reg_in[5]), .out(multiplexer_3_out), .sel(reg_in_en));
  D_Flip_Flop d_ff_3 (.D(multiplexer_3_out), .clk(reg_clk), .Q(reg_int_out[5]));  // open: Qn, preset, reset
  Multiplexer multiplexer_4 (.in0(reg_int_out[4]), .in1(reg_in[4]), .out(multiplexer_4_out), .sel(reg_in_en));
  assign reg_out[5] = reg_out_en ? reg_int_out[5] : 1'bz;  // Controlled_Buffer controlled_buffer_3
  D_Flip_Flop d_ff_4 (.D(multiplexer_4_out), .clk(reg_clk), .Q(reg_int_out[4]));  // open: Qn, preset, reset
  Multiplexer multiplexer_5 (.in0(reg_int_out[3]), .in1(reg_in[3]), .out(multiplexer_5_out), .sel(reg_in_en));
  D_Flip_Flop d_ff_5 (.D(multiplexer_5_out), .clk(reg_clk), .Q(reg_int_out[3]));  // open: Qn, preset, reset
  assign reg_out[4] = reg_out_en ? reg_int_out[4] : 1'bz;  // Controlled_Buffer controlled_buffer_4
  assign reg_out[3] = reg_out_en ? reg_int_out[3] : 1'bz;  // Controlled_Buffer controlled_buffer_5
  Multiplexer multiplexer_6 (.in0(reg_int_out[2]), .in1(reg_in[2]), .out(multiplexer_6_out), .sel(reg_in_en));
  D_Flip_Flop d_ff_6 (.D(multiplexer_6_out), .clk(reg_clk), .Q(reg_int_out[2]));  // open: Qn, preset, reset
  assign reg_out[2] = reg_out_en ? reg_int_out[2] : 1'bz;  // Controlled_Buffer controlled_buffer_6
  Multiplexer multiplexer_7 (.in0(reg_int_out[1]), .in1(reg_in[1]), .out(multiplexer_7_out), .sel(reg_in_en));
  D_Flip_Flop d_ff_7 (.D(multiplexer_7_out), .clk(reg_clk), .Q(reg_int_out[1]));  // open: Qn, preset, reset
  assign reg_out[1] = reg_out_en ? reg_int_out[1] : 1'bz;  // Controlled_Buffer controlled_buffer_7
  Multiplexer multiplexer_8 (.in0(reg_int_out[0]), .in1(reg_in[0]), .out(multiplexer_8_out), .sel(reg_in_en));
  D_Flip_Flop d_ff_8 (.D(multiplexer_8_out), .clk(reg_clk), .Q(reg_int_out[0]));  // open: Qn, preset, reset
  assign reg_out[0] = reg_out_en ? reg_int_out[0] : 1'bz;  // Controlled_Buffer controlled_buffer_8
endmodule

module alu (
  input  [7:0] alu_in_1,
  input  alu_out_en,
  input  alu_sub,
  input  [7:0] alu_in_2,
  output [7:0] alu_out,
  output alu_carry_out
);

  wire adder_2_cout, adder_3_cout, adder_4_cout, adder_5_cout, adder_6_cout, adder_7_cout, adder_8_cout,
       xor_1_out, xor_2_out, xor_3_out, xor_4_out, xor_5_out, xor_6_out, xor_7_out, xor_8_out;
  wire [7:0] adder_8_out;

  Adder #(.width(1)) adder_1 (
    .a(alu_in_1[7]), .b(xor_1_out), .out(adder_8_out[7]), .cin(adder_2_cout), .cout(alu_carry_out));
  xor xor_1 (xor_1_out, alu_in_2[7], alu_sub);
  xor xor_2 (xor_2_out, alu_in_2[6], alu_sub);
  Adder #(.width(1)) adder_2 (
    .a(alu_in_1[6]), .b(xor_2_out), .out(adder_8_out[6]), .cin(adder_3_cout), .cout(adder_2_cout));
  xor xor_3 (xor_3_out, alu_in_2[5], alu_sub);
  Adder #(.width(1)) adder_3 (
    .a(alu_in_1[5]), .b(xor_3_out), .out(adder_8_out[5]), .cin(adder_4_cout), .cout(adder_3_cout));
  Adder #(.width(1)) adder_4 (
    .a(alu_in_1[4]), .b(xor_4_out), .out(adder_8_out[4]), .cin(adder_5_cout), .cout(adder_4_cout));
  xor xor_4 (xor_4_out, alu_in_2[4], alu_sub);
  Adder #(.width(1)) adder_5 (
    .a(alu_in_1[3]), .b(xor_5_out), .out(adder_8_out[3]), .cin(adder_6_cout), .cout(adder_5_cout));
  xor xor_5 (xor_5_out, alu_in_2[3], alu_sub);
  xor xor_6 (xor_6_out, alu_in_2[2], alu_sub);
  Adder #(.width(1)) adder_6 (
    .a(alu_in_1[2]), .b(xor_6_out), .out(adder_8_out[2]), .cin(adder_7_cout), .cout(adder_6_cout));
  xor xor_7 (xor_7_out, alu_in_2[1], alu_sub);
  Adder #(.width(1)) adder_7 (
    .a(alu_in_1[1]), .b(xor_7_out), .out(adder_8_out[1]), .cin(adder_8_cout), .cout(adder_7_cout));
  Adder #(.width(1)) adder_8 (.a(alu_in_1[0]), .b(xor_8_out), .out(adder_8_out[0]), .cin(alu_sub), .cout(adder_8_cout));
  xor xor_8 (xor_8_out, alu_in_2[0], alu_sub);
  assign alu_out = alu_out_en ? adder_8_out : 8'bz;  // Controlled_Buffer controlled_buffer_1
endmodule

module pc (
  input  pc_en,
  input  pc_clk,
  input  pc_reset,
  input  pc_out_en,
  output [3:0] pc_out
);

  wire j_k_ff_2_qn, j_k_ff_3_qn, j_k_ff_4_qn;
  wire [3:0] j_k_ff_4_q;

  J_K_Flip_Flop j_k_ff_1 (
    .J(pc_en), .K(pc_en), .clk(j_k_ff_2_qn), .Q(j_k_ff_4_q[3]), .reset(pc_reset));  // open: Qn, preset
  J_K_Flip_Flop j_k_ff_2 (
    .J(pc_en), .K(pc_en), .clk(j_k_ff_3_qn), .Q(j_k_ff_4_q[2]), .Qn(j_k_ff_2_qn), .reset(pc_reset));  // open: preset
  J_K_Flip_Flop j_k_ff_3 (
    .J(pc_en), .K(pc_en), .clk(j_k_ff_4_qn), .Q(j_k_ff_4_q[1]), .Qn(j_k_ff_3_qn), .reset(pc_reset));  // open: preset
  J_K_Flip_Flop j_k_ff_4 (
    .J(pc_en), .K(pc_en), .clk(pc_clk), .Q(j_k_ff_4_q[0]), .Qn(j_k_ff_4_qn), .reset(pc_reset));  // open: preset
  assign pc_out = pc_out_en ? j_k_ff_4_q : 4'bz;  // Controlled_Buffer controlled_buffer_1
endmodule

module sram_cell (
  input  [7:0] data_en,
  input  wr_en,
  input  clk,
  input  cs,
  input  rd_en,
  output [7:0] memory_content,
  output [7:0] data_out
);

  wire and_1_out, and_2_out;

  and and_1 (and_1_out, wr_en, cs);
  and and_2 (and_2_out, cs, rd_en);
  reg_gp reg_gp_1 (
    .reg_in(data_en), .reg_in_en(and_1_out), .reg_clk(clk), .reg_out_en(and_2_out),
    .reg_int_out(memory_content), .reg_out(data_out));
endmodule

module ins_reg (
  input  [7:0] ins_reg_in,
  input  ins_reg_in_en,
  input  clk,
  input  address_out_en,
  output [3:0] add_outs,
  output [3:0] ins_out
);

  wire [3:0] reg_gp_1_reg_int_out;

  reg_gp reg_gp_1 (
    .reg_in(ins_reg_in), .reg_in_en(ins_reg_in_en), .reg_clk(clk),
    .reg_int_out({ins_out, reg_gp_1_reg_int_out}));  // open: reg_out_en, reg_out
  assign add_outs = address_out_en ? reg_gp_1_reg_int_out : 4'bz;  // Controlled_Buffer controlled_buffer_1
endmodule

module sram (
  input  sram_rd,
  input  sram_wr,
  input  [7:0] sram_d_in,
  input  [7:0] mar_d_in,
  input  mar_in_en,
  input  sram_clk,
  output [7:0] out_7,
  output [7:0] out_8,
  output [7:0] out_9,
  output [7:0] out_10,
  output [7:0] out_11,
  output [7:0] out_12,
  output [7:0] out_13,
  output [7:0] out_14,
  output [7:0] out_15,
  output [7:0] out_16,
  output [7:0] out_17,
  output [7:0] out_18,
  output [7:0] out_19,
  output [7:0] out_20,
  output [7:0] out_21,
  output [7:0] out_22,
  output [7:0] out_23
);

  wire [7:0] controlled_buffer_1_out, reg_gp_1_reg_int_out;
  wire [15:0] dec_4x16_1_dec_out;

  dec_4x16 dec_4x16_1 (.in_1(reg_gp_1_reg_int_out[3:0]), .dec_out(dec_4x16_1_dec_out));
  reg_gp reg_gp_1 (
    .reg_in(mar_d_in), .reg_in_en(mar_in_en), .reg_clk(sram_clk), .reg_int_out(reg_gp_1_reg_int_out));  // open: reg_out_en, reg_out
  assign controlled_buffer_1_out = sram_wr ? sram_d_in : 8'bz;  // Controlled_Buffer controlled_buffer_1
  assign out_7 = sram_rd ? controlled_buffer_1_out : 8'bz;  // Controlled_Buffer controlled_buffer_2
  sram_cell sram_cell_1 (
    .data_en(controlled_buffer_1_out), .wr_en(sram_wr), .clk(sram_clk), .cs(dec_4x16_1_dec_out[0]),
    .rd_en(sram_rd), .memory_content(out_8), .data_out(controlled_buffer_1_out));
  sram_cell sram_cell_2 (
    .data_en(controlled_buffer_1_out), .wr_en(sram_wr), .clk(sram_clk), .cs(dec_4x16_1_dec_out[1]),
    .rd_en(sram_rd), .memory_content(out_9), .data_out(controlled_buffer_1_out));
  sram_cell sram_cell_3 (
    .data_en(controlled_buffer_1_out), .wr_en(sram_wr), .clk(sram_clk), .cs(dec_4x16_1_dec_out[2]),
    .rd_en(sram_rd), .memory_content(out_10), .data_out(controlled_buffer_1_out));
  sram_cell sram_cell_4 (
    .data_en(controlled_buffer_1_out), .wr_en(sram_wr), .clk(sram_clk), .cs(dec_4x16_1_dec_out[3]),
    .rd_en(sram_rd), .memory_content(out_11), .data_out(controlled_buffer_1_out));
  sram_cell sram_cell_5 (
    .data_en(controlled_buffer_1_out), .wr_en(sram_wr), .clk(sram_clk), .cs(dec_4x16_1_dec_out[4]),
    .rd_en(sram_rd), .memory_content(out_12), .data_out(controlled_buffer_1_out));
  sram_cell sram_cell_6 (
    .data_en(controlled_buffer_1_out), .wr_en(sram_wr), .clk(sram_clk), .cs(dec_4x16_1_dec_out[5]),
    .rd_en(sram_rd), .memory_content(out_13), .data_out(controlled_buffer_1_out));
  sram_cell sram_cell_7 (
    .data_en(controlled_buffer_1_out), .wr_en(sram_wr), .clk(sram_clk), .cs(dec_4x16_1_dec_out[6]),
    .rd_en(sram_rd), .memory_content(out_14), .data_out(controlled_buffer_1_out));
  sram_cell sram_cell_8 (
    .data_en(controlled_buffer_1_out), .wr_en(sram_wr), .clk(sram_clk), .cs(dec_4x16_1_dec_out[7]),
    .rd_en(sram_rd), .memory_content(out_15), .data_out(controlled_buffer_1_out));
  sram_cell sram_cell_9 (
    .data_en(controlled_buffer_1_out), .wr_en(sram_wr), .clk(sram_clk), .cs(dec_4x16_1_dec_out[8]),
    .rd_en(sram_rd), .memory_content(out_16), .data_out(controlled_buffer_1_out));
  sram_cell sram_cell_10 (
    .data_en(controlled_buffer_1_out), .wr_en(sram_wr), .clk(sram_clk), .cs(dec_4x16_1_dec_out[9]),
    .rd_en(sram_rd), .memory_content(out_17), .data_out(controlled_buffer_1_out));
  sram_cell sram_cell_11 (
    .data_en(controlled_buffer_1_out), .wr_en(sram_wr), .clk(sram_clk), .cs(dec_4x16_1_dec_out[10]),
    .rd_en(sram_rd), .memory_content(out_18), .data_out(controlled_buffer_1_out));
  sram_cell sram_cell_12 (
    .data_en(controlled_buffer_1_out), .wr_en(sram_wr), .clk(sram_clk), .cs(dec_4x16_1_dec_out[11]),
    .rd_en(sram_rd), .memory_content(out_19), .data_out(controlled_buffer_1_out));
  sram_cell sram_cell_13 (
    .data_en(controlled_buffer_1_out), .wr_en(sram_wr), .clk(sram_clk), .cs(dec_4x16_1_dec_out[12]),
    .rd_en(sram_rd), .memory_content(out_20), .data_out(controlled_buffer_1_out));
  sram_cell sram_cell_14 (
    .data_en(controlled_buffer_1_out), .wr_en(sram_wr), .clk(sram_clk), .cs(dec_4x16_1_dec_out[13]),
    .rd_en(sram_rd), .memory_content(out_21), .data_out(controlled_buffer_1_out));
  sram_cell sram_cell_15 (
    .data_en(controlled_buffer_1_out), .wr_en(sram_wr), .clk(sram_clk), .cs(dec_4x16_1_dec_out[14]),
    .rd_en(sram_rd), .memory_content(out_22), .data_out(controlled_buffer_1_out));
  sram_cell sram_cell_16 (
    .data_en(controlled_buffer_1_out), .wr_en(sram_wr), .clk(sram_clk), .cs(dec_4x16_1_dec_out[15]),
    .rd_en(sram_rd), .memory_content(out_23), .data_out(controlled_buffer_1_out));
endmodule

module dec_4x16 (
  input  [3:0] in_1,
  output [15:0] dec_out
);

  wire not_1_out, not_2_out, not_3_out, not_4_out;

  not not_1 (not_1_out, in_1[3]);
  not not_2 (not_2_out, in_1[2]);
  not not_3 (not_3_out, in_1[1]);
  not not_4 (not_4_out, in_1[0]);
  and and_1 (dec_out[0], not_4_out, not_3_out, not_2_out, not_1_out);
  and and_2 (dec_out[1], in_1[0], not_3_out, not_2_out, not_1_out);
  and and_3 (dec_out[2], not_4_out, in_1[1], not_2_out, not_1_out);
  and and_4 (dec_out[3], in_1[0], in_1[1], not_2_out, not_1_out);
  and and_5 (dec_out[4], not_4_out, not_3_out, in_1[2], not_1_out);
  and and_6 (dec_out[5], in_1[0], not_3_out, in_1[2], not_1_out);
  and and_7 (dec_out[6], not_4_out, in_1[1], in_1[2], not_1_out);
  and and_8 (dec_out[7], in_1[0], in_1[1], in_1[2], not_1_out);
  and and_9 (dec_out[8], not_4_out, not_3_out, not_2_out, in_1[3]);
  and and_10 (dec_out[9], in_1[0], not_3_out, not_2_out, in_1[3]);
  and and_11 (dec_out[10], not_4_out, in_1[1], not_2_out, in_1[3]);
  and and_12 (dec_out[11], in_1[0], in_1[1], not_2_out, in_1[3]);
  and and_13 (dec_out[12], not_4_out, not_3_out, in_1[2], in_1[3]);
  and and_14 (dec_out[13], in_1[0], not_3_out, in_1[2], in_1[3]);
  and and_15 (dec_out[14], not_4_out, in_1[1], in_1[2], in_1[3]);
  and and_16 (dec_out[15], in_1[0], in_1[1], in_1[2], in_1[3]);
endmodule

module Ctr_seq (
  input  State_en,
  input  clk,
  input  Timing_reset,
  input  [3:0] OPCODE,
  input  mar_in_manual,
  input  sram_wr_manual,
  input  debug,
  output pc_en,
  output mar_in,
  output address_out,
  output pc_out,
  output ins_reg_in,
  output ins_reg_out,
  output pc_load,
  output sram_rd,
  output ro_out_en,
  output b_in,
  output rotate_reg_en,
  output right_or_left,
  output alu_sub,
  output a_in,
  output alu_out,
  output sram_wr
);

  wire and_3_out, and_4_out, and_5_out, and_6_out, and_7_out, and_9_out, and_11_out, and_12_out, and_13_out,
       and_14_out, opcode_decoder_1_hlt, opcode_decoder_1_jump, opcode_decoder_1_lda, opcode_decoder_1_ldb,
       opcode_decoder_1_rol_a, opcode_decoder_1_rol_b, opcode_decoder_1_ror_a, opcode_decoder_1_ror_b,
       opcode_decoder_1_sta, opcode_decoder_1_sts, or_5_out, or_6_out, timing_counter_1_t3_state,
       timing_counter_1_t4_state, undriven;

  Multiplexer multiplexer_1 (.in0(or_5_out), .in1(mar_in_manual), .out(mar_in), .sel(debug));
  or or_1 (sram_rd, and_3_out, alu_sub, and_4_out, and_6_out, ins_reg_in);
  or or_2 (b_in, and_6_out, alu_sub, and_4_out);
  or or_3 (a_in, and_3_out, and_9_out, and_7_out);
  or or_4 (alu_out, and_5_out, and_7_out, and_9_out);
  timing_counter timing_counter_1 (
    .tcount_en(State_en), .clk(clk), .reset(Timing_reset), .T1_state(pc_out), .T2_state(ins_reg_in),
    .T3_state(timing_counter_1_t3_state), .T4_state(timing_counter_1_t4_state));
  opcode_decoder opcode_decoder_1 (
    .inst_opcode(OPCODE), .LDA(opcode_decoder_1_lda), .LDB(opcode_decoder_1_ldb), .STA(opcode_decoder_1_sta),
    .STS(opcode_decoder_1_sts), .ROR_A(opcode_decoder_1_ror_a), .ROR_B(opcode_decoder_1_ror_b),
    .ROL_A(opcode_decoder_1_rol_a), .ROL_B(opcode_decoder_1_rol_b), .JUMP(opcode_decoder_1_jump),
    .HLT(opcode_decoder_1_hlt));
  or or_5 (or_5_out, timing_counter_1_t3_state, pc_out);
  // AND_Gate and_1 is placed but not wired
  and and_2 (address_out, opcode_decoder_1_hlt, timing_counter_1_t3_state);
  and and_3 (and_3_out, opcode_decoder_1_lda, timing_counter_1_t4_state);
  and and_4 (and_4_out, timing_counter_1_t4_state, opcode_decoder_1_ldb);
  and and_5 (and_5_out, opcode_decoder_1_sta, timing_counter_1_t4_state);
  Multiplexer multiplexer_2 (.in0(and_5_out), .in1(sram_wr_manual), .out(sram_wr), .sel(debug));
  and and_6 (and_6_out, timing_counter_1_t4_state, opcode_decoder_1_sts);
  and and_7 (and_7_out, opcode_decoder_1_sts, undriven);
  and and_8 (alu_sub, opcode_decoder_1_ror_a, timing_counter_1_t4_state);
  and and_9 (and_9_out, opcode_decoder_1_ror_a, undriven);
  or or_6 (or_6_out, opcode_decoder_1_ror_b, opcode_decoder_1_rol_a, opcode_decoder_1_rol_b, opcode_decoder_1_jump);
  and and_10 (ro_out_en, or_6_out, timing_counter_1_t3_state);
  and and_11 (and_11_out, opcode_decoder_1_rol_a, timing_counter_1_t3_state);
  and and_12 (and_12_out, opcode_decoder_1_jump, timing_counter_1_t3_state);
  or or_7 (rotate_reg_en, and_11_out, and_12_out);
  and and_13 (and_13_out, opcode_decoder_1_rol_b, timing_counter_1_t3_state);
  or or_8 (right_or_left, and_13_out, and_14_out);
  and and_14 (and_14_out, opcode_decoder_1_jump, timing_counter_1_t3_state);

  assign ins_reg_out = ins_reg_in;
  assign pc_en = ins_reg_in;
  assign pc_load = address_out;
endmodule

module timing_counter (
  input  tcount_en,
  input  clk,
  input  reset,
  output T1_state,
  output T2_state,
  output T3_state,
  output T4_state
);

  wire controlled_buffer_1_out, not_1_out;
  wire [3:0] pc_1_pc_out;
  wire [15:0] dec_4x16_1_dec_out;

  assign controlled_buffer_1_out = reset ? reset : 1'bz;  // Controlled_Buffer controlled_buffer_1
  assign controlled_buffer_1_out = not_1_out ? dec_4x16_1_dec_out[5] : 1'bz;  // Controlled_Buffer controlled_buffer_2
  not not_1 (not_1_out, reset);
  pc pc_1 (
    .pc_en(tcount_en), .pc_clk(clk), .pc_reset(controlled_buffer_1_out), .pc_out_en(tcount_en),
    .pc_out(pc_1_pc_out));
  dec_4x16 dec_4x16_1 (
    .in_1(pc_1_pc_out),
    .dec_out({dec_4x16_1_dec_out[15:5], T4_state, T3_state, T2_state, T1_state, dec_4x16_1_dec_out[0]}));
endmodule

module opcode_decoder (
  input  [3:0] inst_opcode,
  output LDA,
  output LDB,
  output STA,
  output STS,
  output ROR_A,
  output ROR_B,
  output ROL_A,
  output ROL_B,
  output JUMP,
  output HLT
);

  wire [15:0] dec_4x16_1_dec_out;

  dec_4x16 dec_4x16_1 (
    .in_1(inst_opcode),
    .dec_out({dec_4x16_1_dec_out[15:12], HLT, JUMP, ROL_B, ROL_A, ROR_B, ROR_A, dec_4x16_1_dec_out[5], STS, STA, LDB, LDA, dec_4x16_1_dec_out[0]}));
endmodule

module Shifter8 (
  input  [7:0] B_reg_int_out,
  input  [7:0] A_reg_int_out,
  input  rotate_reg_en,
  input  right_or_left,
  input  ro_out_en,
  output [7:0] ro_out
);

  wire multiplexer_1_out, multiplexer_2_out, multiplexer_3_out, multiplexer_4_out, multiplexer_5_out,
       multiplexer_6_out, multiplexer_7_out, multiplexer_8_out, multiplexer_9_out, multiplexer_10_out,
       multiplexer_11_out, multiplexer_12_out, multiplexer_13_out, multiplexer_14_out, multiplexer_15_out,
       multiplexer_16_out;

  Multiplexer multiplexer_1 (
    .in0(A_reg_int_out[0]), .in1(B_reg_int_out[0]), .out(multiplexer_1_out), .sel(rotate_reg_en));
  Multiplexer multiplexer_2 (
    .in0(multiplexer_3_out), .in1(multiplexer_15_out), .out(multiplexer_2_out), .sel(right_or_left));
  assign ro_out[0] = ro_out_en ? multiplexer_2_out : 1'bz;  // Controlled_Buffer controlled_buffer_1
  Multiplexer multiplexer_3 (
    .in0(A_reg_int_out[1]), .in1(B_reg_int_out[1]), .out(multiplexer_3_out), .sel(rotate_reg_en));
  Multiplexer multiplexer_4 (
    .in0(multiplexer_5_out), .in1(multiplexer_1_out), .out(multiplexer_4_out), .sel(right_or_left));
  assign ro_out[1] = ro_out_en ? multiplexer_4_out : 1'bz;  // Controlled_Buffer controlled_buffer_2
  Multiplexer multiplexer_5 (
    .in0(A_reg_int_out[2]), .in1(B_reg_int_out[2]), .out(multiplexer_5_out), .sel(rotate_reg_en));
  Multiplexer multiplexer_6 (
    .in0(multiplexer_7_out), .in1(multiplexer_3_out), .out(multiplexer_6_out), .sel(right_or_left));
  assign ro_out[2] = ro_out_en ? multiplexer_6_out : 1'bz;  // Controlled_Buffer controlled_buffer_3
  Multiplexer multiplexer_7 (
    .in0(A_reg_int_out[3]), .in1(B_reg_int_out[3]), .out(multiplexer_7_out), .sel(rotate_reg_en));
  Multiplexer multiplexer_8 (
    .in0(multiplexer_9_out), .in1(multiplexer_5_out), .out(multiplexer_8_out), .sel(right_or_left));
  assign ro_out[3] = ro_out_en ? multiplexer_8_out : 1'bz;  // Controlled_Buffer controlled_buffer_4
  Multiplexer multiplexer_9 (
    .in0(A_reg_int_out[4]), .in1(B_reg_int_out[4]), .out(multiplexer_9_out), .sel(rotate_reg_en));
  Multiplexer multiplexer_10 (
    .in0(multiplexer_11_out), .in1(multiplexer_7_out), .out(multiplexer_10_out), .sel(right_or_left));
  assign ro_out[4] = ro_out_en ? multiplexer_10_out : 1'bz;  // Controlled_Buffer controlled_buffer_5
  Multiplexer multiplexer_11 (
    .in0(A_reg_int_out[5]), .in1(B_reg_int_out[5]), .out(multiplexer_11_out), .sel(rotate_reg_en));
  Multiplexer multiplexer_12 (
    .in0(multiplexer_13_out), .in1(multiplexer_9_out), .out(multiplexer_12_out), .sel(right_or_left));
  assign ro_out[5] = ro_out_en ? multiplexer_12_out : 1'bz;  // Controlled_Buffer controlled_buffer_6
  Multiplexer multiplexer_13 (
    .in0(A_reg_int_out[6]), .in1(B_reg_int_out[6]), .out(multiplexer_13_out), .sel(rotate_reg_en));
  Multiplexer multiplexer_14 (
    .in0(multiplexer_15_out), .in1(multiplexer_11_out), .out(multiplexer_14_out), .sel(right_or_left));
  assign ro_out[6] = ro_out_en ? multiplexer_14_out : 1'bz;  // Controlled_Buffer controlled_buffer_7
  Multiplexer multiplexer_15 (
    .in0(A_reg_int_out[7]), .in1(B_reg_int_out[7]), .out(multiplexer_15_out), .sel(rotate_reg_en));
  Multiplexer multiplexer_16 (
    .in0(multiplexer_1_out), .in1(multiplexer_13_out), .out(multiplexer_16_out), .sel(right_or_left));
  assign ro_out[7] = ro_out_en ? multiplexer_16_out : 1'bz;  // Controlled_Buffer controlled_buffer_8
endmodule

module pc_with_loader (
  input  pc_en,
  input  [3:0] pc_in,
  input  pc_load,
  input  clk,
  input  pc_reset,
  input  pc_out_en,
  output [3:0] pc_out
);

  wire and_1_out, and_2_out, and_3_out, and_4_out, and_5_out, multiplexer_1_out, multiplexer_2_out,
       multiplexer_3_out, multiplexer_4_out, multiplexer_5_out, multiplexer_6_out, multiplexer_7_out,
       multiplexer_8_out, not_1_out, not_2_out, not_3_out, not_4_out;
  wire [3:0] j_k_ff_1_q;

  not not_1 (not_1_out, pc_in[0]);
  Multiplexer multiplexer_1 (.in0(pc_en), .in1(pc_in[0]), .out(multiplexer_1_out), .sel(pc_load));
  Multiplexer multiplexer_2 (.in0(pc_en), .in1(not_1_out), .out(multiplexer_2_out), .sel(pc_load));
  J_K_Flip_Flop j_k_ff_1 (
    .J(multiplexer_1_out), .K(multiplexer_2_out), .clk(clk), .Q(j_k_ff_1_q[0]), .reset(pc_reset));  // open: Qn, preset
  and and_1 (and_1_out, j_k_ff_1_q[0], pc_en);
  Multiplexer multiplexer_3 (.in0(and_1_out), .in1(pc_in[1]), .out(multiplexer_3_out), .sel(pc_load));
  Multiplexer multiplexer_4 (.in0(and_1_out), .in1(not_2_out), .out(multiplexer_4_out), .sel(pc_load));
  not not_2 (not_2_out, pc_in[1]);
  J_K_Flip_Flop j_k_ff_2 (
    .J(multiplexer_3_out), .K(multiplexer_4_out), .clk(clk), .Q(j_k_ff_1_q[1]), .reset(pc_reset));  // open: Qn, preset
  and and_2 (and_2_out, multiplexer_3_out, j_k_ff_1_q[1]);
  and and_3 (and_3_out, and_2_out, pc_en);
  not not_3 (not_3_out, pc_in[2]);
  Multiplexer multiplexer_5 (.in0(and_3_out), .in1(pc_in[2]), .out(multiplexer_5_out), .sel(pc_load));
  J_K_Flip_Flop j_k_ff_3 (
    .J(multiplexer_5_out), .K(multiplexer_6_out), .clk(clk), .Q(j_k_ff_1_q[2]), .reset(pc_reset));  // open: Qn, preset
  Multiplexer multiplexer_6 (.in0(and_3_out), .in1(not_3_out), .out(multiplexer_6_out), .sel(pc_load));
  and and_4 (and_4_out, and_2_out, j_k_ff_1_q[2]);
  not not_4 (not_4_out, pc_in[3]);
  and and_5 (and_5_out, and_4_out, pc_en);
  Multiplexer multiplexer_7 (.in0(and_5_out), .in1(pc_in[3]), .out(multiplexer_7_out), .sel(pc_load));
  Multiplexer multiplexer_8 (.in0(and_5_out), .in1(not_4_out), .out(multiplexer_8_out), .sel(pc_load));
  J_K_Flip_Flop j_k_ff_4 (
    .J(multiplexer_7_out), .K(multiplexer_8_out), .clk(clk), .Q(j_k_ff_1_q[3]), .reset(pc_reset));  // open: Qn, preset
  assign pc_out = pc_out_en ? j_k_ff_1_q : 4'bz;  // Controlled_Buffer controlled_buffer_1
endmodule

module cs (
  input  clk,
  input  timig_reset,
  input  [3:0] opcode,
  input  switch,
  input  mar_in_manual,
  input  debug,
  input  sram_wr_manual,
  output pc_en,
  output alu_sub,
  output mar_in_en,
  output sram_rd,
  output pc_out,
  output ins_reg_in_en,
  output a_in,
  output b_in,
  output ro_out_en,
  output pc_load,
  output hlt_set,
  output rotate_reg_en,
  output right_or_left,
  output sram_wr,
  output alu_out,
  output address_out_en
);

  wire and_1_out, and_3_out, and_4_out, and_7_out, and_8_out, and_9_out, and_10_out, d_ff_1_q, not_1_out,
       opcode_decoder_1_hlt, opcode_decoder_1_jump, opcode_decoder_1_lda, opcode_decoder_1_ldb,
       opcode_decoder_1_rol_a, opcode_decoder_1_rol_b, opcode_decoder_1_ror_a, opcode_decoder_1_ror_b,
       opcode_decoder_1_sta, opcode_decoder_1_sts, or_1_out, or_2_out, or_3_out, timing_counter_1_t3_state,
       timing_counter_1_t4_state;

  not not_1 (not_1_out, hlt_set);
  and and_1 (and_1_out, d_ff_1_q, not_1_out);
  or or_1 (or_1_out, and_1_out, switch);
  D_Flip_Flop d_ff_1 (.D(or_1_out), .clk(or_2_out), .Q(d_ff_1_q));  // open: Qn, preset, reset
  or or_2 (or_2_out, switch, clk);
  Multiplexer multiplexer_1 (.in0(or_3_out), .in1(mar_in_manual), .out(mar_in_en), .sel(debug));
  or or_3 (or_3_out, pc_out, timing_counter_1_t3_state);
  or or_4 (sram_rd, ins_reg_in_en, b_in, a_in);
  timing_counter timing_counter_1 (
    .tcount_en(d_ff_1_q), .clk(clk), .reset(timig_reset), .T1_state(pc_out), .T2_state(ins_reg_in_en),
    .T3_state(timing_counter_1_t3_state), .T4_state(timing_counter_1_t4_state));
  opcode_decoder opcode_decoder_1 (
    .inst_opcode(opcode), .LDA(opcode_decoder_1_lda), .LDB(opcode_decoder_1_ldb), .STA(opcode_decoder_1_sta),
    .STS(opcode_decoder_1_sts), .ROR_A(opcode_decoder_1_ror_a), .ROR_B(opcode_decoder_1_ror_b),
    .ROL_A(opcode_decoder_1_rol_a), .ROL_B(opcode_decoder_1_rol_b), .JUMP(opcode_decoder_1_jump),
    .HLT(opcode_decoder_1_hlt));
  Multiplexer multiplexer_2 (.in0(alu_out), .in1(sram_wr_manual), .out(sram_wr), .sel(debug));
  and and_2 (alu_sub, opcode_decoder_1_sts, timing_counter_1_t4_state);
  and and_3 (and_3_out, opcode_decoder_1_sta, timing_counter_1_t4_state);
  or or_5 (alu_out, alu_sub, and_3_out);
  and and_4 (and_4_out, opcode_decoder_1_hlt, timing_counter_1_t4_state);
  or or_6 (address_out_en, timing_counter_1_t3_state, pc_load);
  buf or_7 (hlt_set, and_4_out);  // OR_Gate
  and and_5 (a_in, opcode_decoder_1_lda, timing_counter_1_t4_state);
  and and_6 (b_in, opcode_decoder_1_ldb, timing_counter_1_t4_state);
  and and_7 (and_7_out, opcode_decoder_1_ror_a, timing_counter_1_t4_state);
  or or_8 (ro_out_en, and_7_out, and_8_out, and_9_out, and_10_out);
  and and_8 (and_8_out, opcode_decoder_1_ror_b, timing_counter_1_t4_state);
  or or_9 (rotate_reg_en, and_8_out, and_10_out);
  and and_9 (and_9_out, opcode_decoder_1_rol_a, timing_counter_1_t4_state);
  or or_10 (right_or_left, and_9_out, and_10_out);
  and and_10 (and_10_out, opcode_decoder_1_rol_b, timing_counter_1_t4_state);
  and and_11 (pc_load, opcode_decoder_1_jump, timing_counter_1_t4_state);

  assign pc_en = ins_reg_in_en;
endmodule

module bootloader (
  input  pc_en,
  input  clk,
  input  pc_reset,
  input  pc_out,
  input  debug,
  output [7:0] rom_output
);

  wire controlled_buffer_1_out, d_ff_1_q, not_1_out;
  wire [3:0] pc_1_pc_out;
  wire [7:0] rom_1_data;

  pc pc_1 (.pc_en(pc_en), .pc_clk(clk), .pc_reset(pc_reset), .pc_out_en(pc_out), .pc_out(pc_1_pc_out));
  ROM #(.addrWidth(4)) rom_1 (.addr(pc_1_pc_out), .data(rom_1_data));
  D_Flip_Flop d_ff_1 (.D(controlled_buffer_1_out), .clk(clk), .Q(d_ff_1_q));  // open: Qn, preset, reset
  assign controlled_buffer_1_out = debug ? not_1_out : 1'bz;  // Controlled_Buffer controlled_buffer_1
  not not_1 (not_1_out, d_ff_1_q);
  assign rom_output = not_1_out ? rom_1_data : 8'bz;  // Controlled_Buffer controlled_buffer_2
  // AND_Gate and_1 has open pins: in0=not_1_out, in1=debug, out=open
  // AND_Gate and_2 has open pins: in0=debug, in1=d_ff_1_q, out=open
endmodule
